# Fritzing sketch sanitizerDispenserV1.0 (saved by Fritzing 0.9.3b)
breadboards: 1

parts:
  Part1 = Arduino Nano (Rev3.0)
  Proximity_Sensor = hc-sr04 [part_number=HR-SR04]
  Dispensing = smd LED [color="Red (660nm)" package="1206 [SMD]"]
  Ready = smd LED [color="Green (570nm)" package="1206 [SMD]"]
  Reading = smd LED [color="Yellow (595nm)" package="1206 [SMD]"]
  Immersible_Pump = DC Motor [part_number="DFRobot FIT0563"]
  R1-R3 = Resistor [tolerance=±5% resistance=220 package=THT]
  R2 = Resistor [tolerance=±5% resistance=220 package=THT]
  R3 = Resistor [tolerance=±5% resistance=220 package=THT]
  6VDC_Input = Power plug
  Q1 = Basic FET N-Channel [package="TO220 [THT]"]
  D1 = Rectifier Diode [part_number=1N4001 package="300 mil [THT]"]

nets:
  GND: Part1.GND, Proximity_Sensor.GND, R1-R3.Pin_0, R2.Pin_0, R3.Pin_0, 6VDC_Input.GND, Q1.source
  N1: Part1.D2, Ready.anode
  N2: Part1.D3, Reading.anode
  N3: Part1.D4, Dispensing.anode
  N4: Part1.D5, Q1.gate
  N5: Part1.D7, Proximity_Sensor.Echo
  N6: Part1.D8, Proximity_Sensor.Trig
  VIN: Part1.VIN, Immersible_Pump.pin_1, 6VDC_Input.VCC, D1.cathode
  5V: Part1.5V, Proximity_Sensor.VCC
  N7: Dispensing.cathode, R2.Pin_1
  N8: Ready.cathode, R1-R3.Pin_1
  N9: Reading.cathode, R3.Pin_1
  N10: Immersible_Pump.pin_2, Q1.drain, D1.anode
