# Fritzing sketch sanitizerDispenserV1.1 (saved by Fritzing 0.9.3b)
breadboards: 1

parts:
  part = Arduino Nano (Rev3.0)
  Proximity_Sensor = hc-sr04 [part_number=HR-SR04]
  Dispensing = smd LED [color="Red (660nm)" package="1206 [SMD]"]
  Ready = smd LED [color="Green (570nm)" package="1206 [SMD]"]
  Reading = smd LED [color="Yellow (595nm)" package="1206 [SMD]"]
  Immersible_Pump = DC Motor [part_number="DFRobot FIT0563"]
  R1 = Resistor [tolerance=±5% resistance=220 package=THT]
  R2 = Resistor [tolerance=±5% resistance=220 package=THT]
  R3 = Resistor [tolerance=±5% resistance=220 package=THT]
  6VDC_Input = Power plug
  Mosfet = Basic FET N-Channel [part_number=IRLB8721 package="TO220 [THT]"]
  D1 = Rectifier Diode [part_number=1N4001 package="300 mil [THT]"]

nets:
  GND: part.GND, Proximity_Sensor.GND, R1.Pin_0, R2.Pin_0, R3.Pin_0, 6VDC_Input.GND, Mosfet.source
  N1: part.D2, Ready.anode
  N2: part.D3, Reading.anode
  N3: part.D4, Dispensing.anode
  N4: part.D5, Mosfet.gate
  N5: part.D7, Proximity_Sensor.Echo
  N6: part.D8, Proximity_Sensor.Trig
  VIN: part.VIN, Immersible_Pump.pin_1, 6VDC_Input.VCC, D1.cathode
  5V: part.5V, Proximity_Sensor.VCC
  N7: Dispensing.cathode, R3.Pin_1
  N8: Ready.cathode, R1.Pin_1
  N9: Reading.cathode, R2.Pin_1
  N10: Immersible_Pump.pin_2, Mosfet.drain, D1.anode

notes:
  sanitizerDispenser v 1.0
  Hack The Northeast Beyond
  Travis Lisk - arduino@liskfamily.com
  January 15-17, 2021
  Hand Sanitizer Dispenser
